# Fritzing sketch depth-repeater-board (saved by Fritzing 0.9.3b)
stripboards: 1

parts:
  J1 = Camdenboss CTB0158-2 [part_number=CTB0158-2 package=THT]
  J2 = Camdenboss CTB0158-2 [part_number=CTB0158-2 package=THT]
  J3 = Camdenboss CTB0158-2 [part_number=CTB0158-2 package=THT]
  Nano1 = Arduino Nano v2.3
  J4 = Camdenboss CTB0158-2 [part_number=CTB0158-2 package=THT]
  U1 = MAX485 [package=dil08]
  IC1 = Voltage Regulator [package=78xxl]

nets:
  N1: J1.pin1, Nano1.D12
  N2: J1.pin2, Nano1.D3
  GND: J2.pin1, J3.pin1, Nano1.GND, U1.GND, IC1.GND
  N3: J2.pin2, J3.pin2, IC1.IN
  N4: Nano1.D0RX, U1.RO
  N5: Nano1.D2, U1.RE
  +5V: Nano1.+5V, U1.VCC, IC1.OUT
  N6: J4.pin1, U1.B
  N7: J4.pin2, U1.A
