# Fritzing sketch depth_repeater (saved by Fritzing 0.9.3b)
circuit board: 8.46667cm x 5.64444cm

parts:
  Part1 = Arduino Pro Mini (5V)
  IC1 = Voltage Regulator [package=to220-igo]
  C1 = Ceramic Capacitor [capacitance=100nF package="200 mil [THT, multilayer]"]
  JP1 = Header 4 [package=screwterminal-3.5mm-4_lock]
  JP2 = Header 4 [package=screwterminal-3.5mm-4_lock]
  U1 = MAX485 [package=dil08]

nets:
  N1: Part1.RXI, U1.RO
  VCC: Part1.VCC, C1.1, U1.VCC
  GND: Part1.GND, IC1.GND, C1.0, JP1.4, JP2.1, U1.GND
  N2: Part1.D5, U1.DE
  N3: Part1.D4, U1.RE
  N4: Part1.D3, JP2.3
  N5: Part1.D2, JP2.2
  N6: IC1.IN, JP1.1, JP2.4
  N7: JP1.2, U1.A
  N8: JP1.3, U1.B
